// Logisim project async_counter.circ as structural Verilog: 1 circuit, main circuit main
module main (
);

  wire button_1_out, clock_1_out;
  wire [3:0] j_k_ff_1_q;

  J_K_Flip_Flop #(.trigger("falling")) j_k_ff_1 (
    .J(1'b1), .K(1'b1), .clk(clock_1_out), .Q(j_k_ff_1_q[0]), .reset(button_1_out));  // open: Qn, preset
  Clock clock_1 (.out(clock_1_out));
  Button button_1 (.out(button_1_out));
  Hex_Digit_Display hex_digit_display_1 (.value(j_k_ff_1_q));  // open: dp
  J_K_Flip_Flop #(.trigger("falling")) j_k_ff_2 (
    .J(1'b1), .K(1'b1), .clk(j_k_ff_1_q[0]), .Q(j_k_ff_1_q[1]), .reset(button_1_out));  // open: Qn, preset
  J_K_Flip_Flop #(.trigger("falling")) j_k_ff_3 (
    .J(1'b1), .K(1'b1), .clk(j_k_ff_1_q[1]), .Q(j_k_ff_1_q[2]), .reset(button_1_out));  // open: Qn, preset
  J_K_Flip_Flop #(.trigger("falling")) j_k_ff_4 (
    .J(1'b1), .K(1'b1), .clk(j_k_ff_1_q[2]), .Q(j_k_ff_1_q[3]), .reset(button_1_out));  // open: Qn, preset

  // Notes on the sheet:
  //   CLEAR
  //   4-Bit J-K Flip-Flop
  //   Asynchronous (Ripple) Counter
endmodule
